# Fritzing sketch semafor (saved by Fritzing 0.9.3b)
circuit board: 6cm x 10cm
breadboards: 1

parts:
  R1 = Resistor [tolerance=±5% resistance=330 package=THT]
  LED1 = LED - 5mm [color="Red (635nm)" package="5 mm [THT]"]
  Part1 = Arduino Nano (Rev3.0)
  R3 = Resistor [tolerance=±5% resistance=330 package=THT]
  R4 = Resistor [tolerance=±5% resistance=10k package=THT]
  R2 = Resistor [tolerance=±5% resistance=330 package=THT]
  LED3 = LED - 5mm [color="Green (565nm)" package="5 mm [THT]"]
  LED2 = LED - 5mm [color="Yellow (595nm)" package="5 mm [THT]"]
  S1 = Pushbutton [package="[THT]"]

nets:
  N1: R1.Pin_0, Part1.GND, R3.Pin_0, R4.Pin_0, R2.Pin_0
  N2: R1.Pin_1, LED1.cathode
  N3: LED1.anode, Part1.D3
  N4: Part1.D5, LED2.anode
  N5: Part1.D7, LED3.anode
  N6: Part1.D9, R4.Pin_1, S1.Pin_1, S1.Pin_2
  N7: Part1.3V3, S1.Pin_3, S1.Pin_4
  N8: R3.Pin_1, LED3.cathode
  N9: R2.Pin_1, LED2.cathode

// code stored in the sketch: semafor.ino
//projekt "Semafor" created@sileONmBot

const int crvenaLed= 3;  // Pin za crvenu LED
const int zutaLed = 5;     // Pin za zutu LED
const int zelenaLed = 7;   // Pin za zelenu LED
const int tasterPin = 9;  // Pin za taster Ulaz
int tasterPolozaj;  // Ocitavanje tastera
int zadnjiTasterPolozaj = LOW;   // Zadnje stanje tastera
int semafor = 0;   // Trenutno  stanje semafora

// Slijedece Variable su tipa kao i funkcija millis() koja daje vrijeme za stopericu.

unsigned long zadnjeVrijeme = 0; // ponisti stopericu
unsigned long ispeglaj = 100;   // Ispeglaj signal

void setup() {               

 // Inicijalizacija Pinova
  pinMode(crvenaLed, OUTPUT);
  pinMode(zutaLed, OUTPUT);
  pinMode(zelenaLed, OUTPUT);
  pinMode(tasterPin, INPUT);

 // ugasi semafor
  digitalWrite(crvenaLed, LOW);
  digitalWrite(zutaLed, LOW);
  digitalWrite(zelenaLed, LOW);
}

void loop() {   // glavna petlja programa


tasterPolozaj = digitalRead (tasterPin); // Ovdje se ocitava polozaj tastera na pinu 9

 if ( tasterPolozaj != zadnjiTasterPolozaj ) {  // ponisti stopericu
    zadnjeVrijeme = millis();  // postavi trenutno vrijeme kao zadnjeVrijeme 
    zadnjiTasterPolozaj = tasterPolozaj; 
 }

   if (( ( millis () - zadnjeVrijeme ) > ispeglaj ) && tasterPolozaj == HIGH ) {

   semafor = 1; // upali semafor
   }
   if (semafor == 1 ) {
    // semafor radi ako je pritisnut taster
   
     delay (500); // sacekaj malo
     digitalWrite(crvenaLed, HIGH);  // upali crveno
     delay (5000); // sacekaj 5 sekundi
     digitalWrite(zutaLed, HIGH); //upali zuto
     delay (1000); // sacekaj 1 sekundu
     digitalWrite(crvenaLed, LOW);  //ugasi crveno
     digitalWrite(zutaLed, LOW);  //ugasi zuto
     digitalWrite(zelenaLed, HIGH); 
     delay (8000); // sacekaj 8 sekundi
     digitalWrite(zelenaLed, LOW);
     digitalWrite(zutaLed, HIGH); //upali zuto 
     delay (2000); // sacekaj 1 sekundu
     digitalWrite(zutaLed, LOW);
     digitalWrite(crvenaLed, HIGH);  // upali crveno
     delay (5000); // sacekaj 5 sekundi
     digitalWrite(crvenaLed, LOW)  ;
     semafor = 0; // semafor ugasen
    } 
}

// code stored in the sketch: Semafor_upravljanje sa tasterom.ino
//projekt "Semafor" created@sileONmBot

const int crvenaLed= 3;  // Pin za crvenu LED
const int zutaLed = 5;     // Pin za zutu LED
const int zelenaLed = 7;   // Pin za zelenu LED
const int tasterPin = 9;  // Pin za taster Ulaz
int tasterPolozaj;  // Ocitavanje tastera
int zadnjiTasterPolozaj = LOW;   // Zadnje stanje tastera
int semafor = 0;   // Trenutno  stanje semafora

// Slijedece Variable su tipa kao i funkcija millis() koja daje vrijeme za stopericu.
unsigned long zadnjeVrijeme = 0; // ponisti stopericu
unsigned long ispeglaj = 100;   // Ispeglaj signal

void setup() {               

 // Inicijalizacija Pinova
  pinMode(crvenaLed, OUTPUT);
  pinMode(zutaLed, OUTPUT);
  pinMode(zelenaLed, OUTPUT);
  pinMode(tasterPin, INPUT);

 // ugasi semafor
  digitalWrite(crvenaLed, LOW);
  digitalWrite(zutaLed, LOW);
  digitalWrite(zelenaLed, LOW);
}

void loop() {   // glavna petlja programa

 tasterPolozaj = digitalRead (tasterPin); // Ovdje se ocitava polozaj tastera na pinu 9

 if ( tasterPolozaj != zadnjiTasterPolozaj ) {  // ponisti stopericu ako se promijenio polozaj tastera
    zadnjeVrijeme = millis();  // postavi trenutno vrijeme kao zadnjeVrijeme 
    zadnjiTasterPolozaj = tasterPolozaj;  // zapamti zadnji  polozaj tastera
 }

   if ( ( ( millis () - zadnjeVrijeme ) > ispeglaj ) && tasterPolozaj == HIGH ) {

   semafor = 1;
   }
   if (semafor == 1 ) {
    // semafor radi ako je pritisnut taster
   
     delay (500); // sacekaj malo
     digitalWrite(crvenaLed, HIGH);  // upali crveno
     delay (5000); // sacekaj 5 sekundi
     digitalWrite(zutaLed, HIGH); //upali zuto
     delay (1000); // sacekaj 1 sekundu
     digitalWrite(crvenaLed, LOW);  //ugasi crveno
     digitalWrite(zutaLed, LOW);  //ugasi zuto
     digitalWrite(zelenaLed, HIGH); 
     delay (8000); // sacekaj 8 sekundi
     digitalWrite(zutaLed, HIGH); //upali zuto
     delay (1000); // sacekaj 1 sekundu
     digitalWrite(zelenaLed, LOW);
     delay (1000); // sacekaj 1 sekundu
     digitalWrite(zutaLed, LOW);
     digitalWrite(crvenaLed, HIGH);  // upali crveno
     delay (5000); // sacekaj 5 sekundi
     digitalWrite(crvenaLed, LOW)  ;
     semafor = 0; // semafor ugasen
    } 
}
